// Logisim project SCEVİK_SAYMİS_pro1.circ as structural Verilog
module ALU (
  input  [15:0] INPUT1,
  input  [15:0] INPUT2,
  input  [5:0] ALUOP,
  output ZF,
  output [15:0] OUTPUT
);

  wire and_2_out;
  wire [15:0] adder_1_out, adder_2_out, and_1_out, multiplexer_1_out, multiplexer_2_out, not_1_out, or_1_out,
       subtractor_1_out, subtractor_2_out, xor_1_out;

  Adder #(.width(16)) adder_1 (.a(INPUT1), .b(INPUT2), .out(adder_1_out));  // open: cin, cout
  Subtractor #(.width(16)) subtractor_1 (.a(INPUT1), .b(INPUT2), .out(subtractor_1_out));  // open: bin, bout
  assign and_1_out = INPUT1 & INPUT2;  // AND_Gate and_1, 16 bits wide
  assign or_1_out = INPUT1 | INPUT2;  // OR_Gate or_1, 16 bits wide
  assign not_1_out = ~INPUT2;  // NOT_Gate not_1, 16 bits wide
  Adder #(.width(16)) adder_2 (.a(INPUT2), .b(16'h1), .out(adder_2_out));  // open: cin, cout
  Subtractor #(.width(16)) subtractor_2 (.a(INPUT2), .b(16'h1), .out(subtractor_2_out));  // open: bin, bout
  assign xor_1_out = INPUT1 ^ INPUT2;  // XOR_Gate xor_1, 16 bits wide
  Multiplexer #(.select(3), .width(16), .enable("false")) multiplexer_1 (
    .in0(adder_1_out), .in1(subtractor_1_out), .in2(and_1_out), .in3(or_1_out), .in4(xor_1_out),
    .out(multiplexer_1_out), .sel(ALUOP[5:3]));  // open: in5, in6, in7
  Multiplexer #(.select(3), .width(16), .enable("false")) multiplexer_2 (
    .in0(not_1_out), .in1(INPUT2), .in2(adder_2_out), .in3(subtractor_2_out), .out(multiplexer_2_out),
    .sel(ALUOP[2:0]));  // open: in4, in5, in6, in7
  and and_2 (and_2_out, ALUOP[3], ALUOP[4], ALUOP[5]);
  Multiplexer #(.width(16), .enable("false")) multiplexer_3 (
    .in0(multiplexer_1_out), .in1(multiplexer_2_out), .out(OUTPUT), .sel(and_2_out));
  nor nor_1 (ZF, OUTPUT[0], OUTPUT[1], OUTPUT[2], OUTPUT[3], OUTPUT[4], OUTPUT[5], OUTPUT[6], OUTPUT[7], OUTPUT[8], OUTPUT[9], OUTPUT[10], OUTPUT[11], OUTPUT[12], OUTPUT[13], OUTPUT[14], OUTPUT[15]);
endmodule

module \_16BİTREG  (
  input  [15:0] INPUT,
  input  CLK,
  input  LOAD,
  output [15:0] OUTPUT
);

  wire not_1_out, not_2_out, not_3_out, not_4_out, not_5_out, not_6_out, not_7_out, not_8_out, not_9_out,
       not_10_out, not_11_out, not_12_out, not_13_out, not_14_out, not_15_out, not_16_out;

  S_R_Flip_Flop s_r_ff_1 (.S(INPUT[0]), .clk(CLK), .R(not_1_out), .Q(OUTPUT[0]), .en(LOAD));  // open: Qn, preset, reset
  not not_1 (not_1_out, INPUT[0]);
  S_R_Flip_Flop s_r_ff_2 (.S(INPUT[1]), .clk(CLK), .R(not_2_out), .Q(OUTPUT[1]), .en(LOAD));  // open: Qn, preset, reset
  not not_2 (not_2_out, INPUT[1]);
  S_R_Flip_Flop s_r_ff_3 (.S(INPUT[2]), .clk(CLK), .R(not_3_out), .Q(OUTPUT[2]), .en(LOAD));  // open: Qn, preset, reset
  not not_3 (not_3_out, INPUT[2]);
  S_R_Flip_Flop s_r_ff_4 (.S(INPUT[3]), .clk(CLK), .R(not_4_out), .Q(OUTPUT[3]), .en(LOAD));  // open: Qn, preset, reset
  not not_4 (not_4_out, INPUT[3]);
  S_R_Flip_Flop s_r_ff_5 (.S(INPUT[4]), .clk(CLK), .R(not_5_out), .Q(OUTPUT[4]), .en(LOAD));  // open: Qn, preset, reset
  not not_5 (not_5_out, INPUT[4]);
  S_R_Flip_Flop s_r_ff_6 (.S(INPUT[5]), .clk(CLK), .R(not_6_out), .Q(OUTPUT[5]), .en(LOAD));  // open: Qn, preset, reset
  not not_6 (not_6_out, INPUT[5]);
  S_R_Flip_Flop s_r_ff_7 (.S(INPUT[6]), .clk(CLK), .R(not_7_out), .Q(OUTPUT[6]), .en(LOAD));  // open: Qn, preset, reset
  not not_7 (not_7_out, INPUT[6]);
  S_R_Flip_Flop s_r_ff_8 (.S(INPUT[7]), .clk(CLK), .R(not_8_out), .Q(OUTPUT[7]), .en(LOAD));  // open: Qn, preset, reset
  not not_8 (not_8_out, INPUT[7]);
  S_R_Flip_Flop s_r_ff_9 (.S(INPUT[8]), .clk(CLK), .R(not_9_out), .Q(OUTPUT[8]), .en(LOAD));  // open: Qn, preset, reset
  not not_9 (not_9_out, INPUT[8]);
  S_R_Flip_Flop s_r_ff_10 (
    .S(INPUT[9]), .clk(CLK), .R(not_10_out), .Q(OUTPUT[9]), .en(LOAD));  // open: Qn, preset, reset
  not not_10 (not_10_out, INPUT[9]);
  S_R_Flip_Flop s_r_ff_11 (
    .S(INPUT[10]), .clk(CLK), .R(not_11_out), .Q(OUTPUT[10]), .en(LOAD));  // open: Qn, preset, reset
  not not_11 (not_11_out, INPUT[10]);
  S_R_Flip_Flop s_r_ff_12 (
    .S(INPUT[11]), .clk(CLK), .R(not_12_out), .Q(OUTPUT[11]), .en(LOAD));  // open: Qn, preset, reset
  not not_12 (not_12_out, INPUT[11]);
  S_R_Flip_Flop s_r_ff_13 (
    .S(INPUT[12]), .clk(CLK), .R(not_13_out), .Q(OUTPUT[12]), .en(LOAD));  // open: Qn, preset, reset
  not not_13 (not_13_out, INPUT[12]);
  S_R_Flip_Flop s_r_ff_14 (
    .S(INPUT[13]), .clk(CLK), .R(not_14_out), .Q(OUTPUT[13]), .en(LOAD));  // open: Qn, preset, reset
  not not_14 (not_14_out, INPUT[13]);
  S_R_Flip_Flop s_r_ff_15 (
    .S(INPUT[14]), .clk(CLK), .R(not_15_out), .Q(OUTPUT[14]), .en(LOAD));  // open: Qn, preset, reset
  not not_15 (not_15_out, INPUT[14]);
  S_R_Flip_Flop s_r_ff_16 (
    .S(INPUT[15]), .clk(CLK), .R(not_16_out), .Q(OUTPUT[15]), .en(LOAD));  // open: Qn, preset, reset
  not not_16 (not_16_out, INPUT[15]);
endmodule

module REGBANK (
  input  LOAD,
  input  [15:0] DataIn,
  input  [2:0] regSelect,
  input  CLK,
  input  SP_plus_plus,
  input  SP_minus_minus,
  output [15:0] Reg0,
  output [15:0] Reg1,
  output [15:0] Reg2,
  output [15:0] Reg3,
  output [15:0] Reg4,
  output [15:0] Reg5,
  output [15:0] Reg6,
  output [15:0] sp
);

  wire and_1_out, and_2_out, and_3_out, and_4_out, and_5_out, and_6_out, and_7_out, and_8_out,
       decoder_1_out0, decoder_1_out1, decoder_1_out2, decoder_1_out3, decoder_1_out4, decoder_1_out5,
       decoder_1_out6, decoder_1_out7, or_1_out, or_2_out;

  Decoder #(.select(3), .enable("false")) decoder_1 (
    .out0(decoder_1_out0), .out1(decoder_1_out1), .out2(decoder_1_out2), .out3(decoder_1_out3),
    .out4(decoder_1_out4), .out5(decoder_1_out5), .out6(decoder_1_out6), .out7(decoder_1_out7),
    .sel(regSelect));
  and and_1 (and_1_out, decoder_1_out7, LOAD);
  or or_1 (or_1_out, SP_minus_minus, SP_plus_plus);
  and and_2 (and_2_out, decoder_1_out0, LOAD);
  and and_3 (and_3_out, decoder_1_out1, LOAD);
  and and_4 (and_4_out, decoder_1_out2, LOAD);
  and and_5 (and_5_out, decoder_1_out3, LOAD);
  and and_6 (and_6_out, decoder_1_out4, LOAD);
  and and_7 (and_7_out, decoder_1_out5, LOAD);
  and and_8 (and_8_out, decoder_1_out6, LOAD);
  or or_2 (or_2_out, and_1_out, or_1_out);
  \_16BİTREG  \u_16bi̇treg_1  (.INPUT(DataIn), .CLK(CLK), .LOAD(and_2_out), .OUTPUT(Reg0));
  \_16BİTREG  \u_16bi̇treg_2  (.INPUT(DataIn), .CLK(CLK), .LOAD(and_3_out), .OUTPUT(Reg1));
  \_16BİTREG  \u_16bi̇treg_3  (.INPUT(DataIn), .CLK(CLK), .LOAD(and_4_out), .OUTPUT(Reg2));
  \_16BİTREG  \u_16bi̇treg_4  (.INPUT(DataIn), .CLK(CLK), .LOAD(and_5_out), .OUTPUT(Reg3));
  \_16BİTREG  \u_16bi̇treg_5  (.INPUT(DataIn), .CLK(CLK), .LOAD(and_6_out), .OUTPUT(Reg4));
  \_16BİTREG  \u_16bi̇treg_6  (.INPUT(DataIn), .CLK(CLK), .LOAD(and_7_out), .OUTPUT(Reg5));
  \_16BİTREG  \u_16bi̇treg_7  (.INPUT(DataIn), .CLK(CLK), .LOAD(and_8_out), .OUTPUT(Reg6));
endmodule

module SPREG (
  input  [15:0] INPUT,
  input  CLK,
  input  LOAD,
  input  SP_plus_plus,
  input  SP_minus_minus,
  output [15:0] OUTPUT
);

  wire or_1_out;
  wire [15:0] adder_1_out, multiplexer_1_out, subtractor_1_out;

  Multiplexer #(.select(2), .width(16), .enable("false")) multiplexer_1 (
    .in0(INPUT), .in1(adder_1_out), .in2(subtractor_1_out), .out(multiplexer_1_out),
    .sel({SP_minus_minus, SP_plus_plus}));  // open: in3
  or or_1 (or_1_out, SP_plus_plus, SP_minus_minus, LOAD);
  \_16BİTREG  \u_16bi̇treg_1  (.INPUT(multiplexer_1_out), .CLK(CLK), .LOAD(or_1_out), .OUTPUT(OUTPUT));
  Subtractor #(.width(16)) subtractor_1 (.a(OUTPUT), .b(16'h1), .out(subtractor_1_out));  // open: bin, bout
  Adder #(.width(16)) adder_1 (.a(OUTPUT), .b(16'h1), .out(adder_1_out));  // open: cin, cout
endmodule

module _12BITREG (
  input  [11:0] INPUT,
  input  CLK,
  input  LOAD,
  output [11:0] OUTPUT
);

  wire not_1_out, not_2_out, not_3_out, not_4_out, not_5_out, not_6_out, not_7_out, not_8_out, not_9_out,
       not_10_out, not_11_out, not_12_out;

  S_R_Flip_Flop s_r_ff_1 (.S(INPUT[0]), .clk(CLK), .R(not_1_out), .Q(OUTPUT[0]), .en(LOAD));  // open: Qn, preset, reset
  not not_1 (not_1_out, INPUT[0]);
  S_R_Flip_Flop s_r_ff_2 (.S(INPUT[1]), .clk(CLK), .R(not_2_out), .Q(OUTPUT[1]), .en(LOAD));  // open: Qn, preset, reset
  not not_2 (not_2_out, INPUT[1]);
  S_R_Flip_Flop s_r_ff_3 (.S(INPUT[2]), .clk(CLK), .R(not_3_out), .Q(OUTPUT[2]), .en(LOAD));  // open: Qn, preset, reset
  not not_3 (not_3_out, INPUT[2]);
  S_R_Flip_Flop s_r_ff_4 (.S(INPUT[3]), .clk(CLK), .R(not_4_out), .Q(OUTPUT[3]), .en(LOAD));  // open: Qn, preset, reset
  not not_4 (not_4_out, INPUT[3]);
  S_R_Flip_Flop s_r_ff_5 (.S(INPUT[4]), .clk(CLK), .R(not_5_out), .Q(OUTPUT[4]), .en(LOAD));  // open: Qn, preset, reset
  not not_5 (not_5_out, INPUT[4]);
  S_R_Flip_Flop s_r_ff_6 (.S(INPUT[5]), .clk(CLK), .R(not_6_out), .Q(OUTPUT[5]), .en(LOAD));  // open: Qn, preset, reset
  not not_6 (not_6_out, INPUT[5]);
  S_R_Flip_Flop s_r_ff_7 (.S(INPUT[6]), .clk(CLK), .R(not_7_out), .Q(OUTPUT[6]), .en(LOAD));  // open: Qn, preset, reset
  not not_7 (not_7_out, INPUT[6]);
  S_R_Flip_Flop s_r_ff_8 (.S(INPUT[7]), .clk(CLK), .R(not_8_out), .Q(OUTPUT[7]), .en(LOAD));  // open: Qn, preset, reset
  not not_8 (not_8_out, INPUT[7]);
  S_R_Flip_Flop s_r_ff_9 (.S(INPUT[8]), .clk(CLK), .R(not_9_out), .Q(OUTPUT[8]), .en(LOAD));  // open: Qn, preset, reset
  not not_9 (not_9_out, INPUT[8]);
  S_R_Flip_Flop s_r_ff_10 (
    .S(INPUT[9]), .clk(CLK), .R(not_10_out), .Q(OUTPUT[9]), .en(LOAD));  // open: Qn, preset, reset
  not not_10 (not_10_out, INPUT[9]);
  S_R_Flip_Flop s_r_ff_11 (
    .S(INPUT[10]), .clk(CLK), .R(not_11_out), .Q(OUTPUT[10]), .en(LOAD));  // open: Qn, preset, reset
  not not_11 (not_11_out, INPUT[10]);
  S_R_Flip_Flop s_r_ff_12 (
    .S(INPUT[11]), .clk(CLK), .R(not_12_out), .Q(OUTPUT[11]), .en(LOAD));  // open: Qn, preset, reset
  not not_12 (not_12_out, INPUT[11]);
endmodule

module PC (
  input  [11:0] INPUT,
  input  CLK,
  input  LOAD,
  input  INC,
  output [11:0] OUTPUT
);

  wire or_1_out;
  wire [11:0] adder_1_out, multiplexer_1_out;

  Multiplexer #(.width(12), .enable("false")) multiplexer_1 (
    .in0(INPUT), .in1(adder_1_out), .out(multiplexer_1_out), .sel(INC));
  or or_1 (or_1_out, INC, LOAD);
  _12BITREG u_12bitreg_1 (.INPUT(multiplexer_1_out), .CLK(CLK), .LOAD(or_1_out), .OUTPUT(OUTPUT));
  Adder #(.width(12)) adder_1 (.a(OUTPUT), .b(12'h1), .out(adder_1_out));  // open: cin, cout
endmodule

module _1BITREG (
  input  CLK,
  input  INPUT,
  input  LOAD,
  output OUTPUT
);

  wire not_1_out;

  S_R_Flip_Flop s_r_ff_1 (.S(INPUT), .clk(CLK), .R(not_1_out), .Q(OUTPUT), .en(LOAD));  // open: Qn, preset, reset
  not not_1 (not_1_out, INPUT);
endmodule

module _4BITREG (
  input  [3:0] INPUT,
  input  CLK,
  input  LOAD,
  output [3:0] OUTPUT
);

  wire not_1_out, not_2_out, not_3_out, not_4_out;

  S_R_Flip_Flop s_r_ff_1 (.S(INPUT[0]), .clk(CLK), .R(not_1_out), .Q(OUTPUT[0]), .en(LOAD));  // open: Qn, preset, reset
  not not_1 (not_1_out, INPUT[0]);
  S_R_Flip_Flop s_r_ff_2 (.S(INPUT[1]), .clk(CLK), .R(not_2_out), .Q(OUTPUT[1]), .en(LOAD));  // open: Qn, preset, reset
  not not_2 (not_2_out, INPUT[1]);
  S_R_Flip_Flop s_r_ff_3 (.S(INPUT[2]), .clk(CLK), .R(not_3_out), .Q(OUTPUT[2]), .en(LOAD));  // open: Qn, preset, reset
  not not_3 (not_3_out, INPUT[2]);
  S_R_Flip_Flop s_r_ff_4 (.S(INPUT[3]), .clk(CLK), .R(not_4_out), .Q(OUTPUT[3]), .en(LOAD));  // open: Qn, preset, reset
  not not_4 (not_4_out, INPUT[3]);
endmodule

module _5BITREG (
  input  [4:0] INPUT,
  input  CLK,
  input  LOAD,
  output [4:0] OUTPUT
);

  wire not_1_out, not_2_out, not_3_out, not_4_out, not_5_out;

  S_R_Flip_Flop s_r_ff_1 (.S(INPUT[0]), .clk(CLK), .R(not_1_out), .Q(OUTPUT[0]), .en(LOAD));  // open: Qn, preset, reset
  not not_1 (not_1_out, INPUT[0]);
  S_R_Flip_Flop s_r_ff_2 (.S(INPUT[1]), .clk(CLK), .R(not_2_out), .Q(OUTPUT[1]), .en(LOAD));  // open: Qn, preset, reset
  not not_2 (not_2_out, INPUT[1]);
  S_R_Flip_Flop s_r_ff_3 (.S(INPUT[2]), .clk(CLK), .R(not_3_out), .Q(OUTPUT[2]), .en(LOAD));  // open: Qn, preset, reset
  not not_3 (not_3_out, INPUT[2]);
  S_R_Flip_Flop s_r_ff_4 (.S(INPUT[3]), .clk(CLK), .R(not_4_out), .Q(OUTPUT[3]), .en(LOAD));  // open: Qn, preset, reset
  not not_4 (not_4_out, INPUT[3]);
  S_R_Flip_Flop s_r_ff_5 (.S(INPUT[4]), .clk(CLK), .R(not_5_out), .Q(OUTPUT[4]), .en(LOAD));  // open: Qn, preset, reset
  not not_5 (not_5_out, INPUT[4]);
endmodule

module CPU (
  input  CLOCK
);

  wire alu_1_zf;
  wire [1:0] n1bitreg_1_output;
  wire [4:0] multiplexer_6_out, multiplexer_7_out, n5bitreg_1_output, rom_1_data_2;
  wire [11:0] adder_1_out, multiplexer_1_out, multiplexer_2_out, multiplexer_5_out, n12bitreg_1_output,
       pc_1_output, regbank_1_sp;
  wire [15:0] alu_1_output, multiplexer_3_out, multiplexer_4_out, ram_1_data, regbank_1_reg0, regbank_1_reg1,
       regbank_1_reg2, regbank_1_reg3, regbank_1_reg4, regbank_1_reg5, regbank_1_reg6;
  wire [15:12] multiplexer_5_out_2, regbank_1_sp_2;
  wire [19:5] rom_1_data;

  Multiplexer #(.width(12), .enable("false")) multiplexer_1 (
    .in0(adder_1_out), .in1(ram_1_data[11:0]), .out(multiplexer_1_out), .sel(rom_1_data[19]));
  PC pc_1 (.INPUT(multiplexer_1_out), .CLK(CLOCK), .LOAD(rom_1_data[16]), .INC(rom_1_data[15]), .OUTPUT(pc_1_output));
  Adder #(.width(12)) adder_1 (.a(pc_1_output), .b(n12bitreg_1_output), .out(adder_1_out));  // open: cin, cout
  Multiplexer #(.select(2), .width(12), .enable("false")) multiplexer_2 (
    .in0(pc_1_output), .in1(multiplexer_5_out), .in2(regbank_1_sp), .out(multiplexer_2_out),
    .sel(rom_1_data[12:11]));  // open: in3
  RAM #(.addrWidth(12), .dataWidth(16), .bus("separate")) ram_1 (
    .addr(multiplexer_2_out), .din(multiplexer_4_out), .data(ram_1_data), .str(rom_1_data[8]), .sel(1'b1),
    .clk(CLOCK), .ld(1'b1), .clr(1'b0));
  REGBANK regbank_1 (
    .LOAD(rom_1_data[5]), .DataIn(multiplexer_4_out), .regSelect(n12bitreg_1_output[2:0]), .CLK(CLOCK),
    .SP_plus_plus(rom_1_data[6]), .Reg0(regbank_1_reg0), .Reg1(regbank_1_reg1), .Reg2(regbank_1_reg2),
    .Reg3(regbank_1_reg3), .Reg4(regbank_1_reg4), .Reg5(regbank_1_reg5), .Reg6(regbank_1_reg6),
    .sp({regbank_1_sp_2, regbank_1_sp}), .SP_minus_minus(rom_1_data[7]));
  isJZ isjz_1 (.in_1(ram_1_data[15:12]), .jz(n1bitreg_1_output[1]));
  Multiplexer #(.select(3), .width(16), .enable("false")) multiplexer_3 (
    .in0(regbank_1_reg0), .in1(regbank_1_reg1), .in2(regbank_1_reg2), .in3(regbank_1_reg3),
    .in4(regbank_1_reg4), .in5(regbank_1_reg5), .in6(regbank_1_reg6), .in7({regbank_1_sp_2, regbank_1_sp}),
    .out(multiplexer_3_out), .sel(n12bitreg_1_output[8:6]));
  Multiplexer #(.select(3), .width(16), .enable("false")) multiplexer_4 (
    .in0(ram_1_data), .in1(multiplexer_3_out), .in2({multiplexer_5_out_2, multiplexer_5_out}),
    .in3(alu_1_output), .in4({4'b0000, pc_1_output}), .out(multiplexer_4_out),
    .sel({rom_1_data[18], rom_1_data[10:9]}));  // open: in5, in6, in7
  ALU alu_1 (
    .INPUT1(multiplexer_3_out), .INPUT2({multiplexer_5_out_2, multiplexer_5_out}),
    .ALUOP(n12bitreg_1_output[11:6]), .ZF(alu_1_zf), .OUTPUT(alu_1_output));
  Multiplexer #(.select(3), .width(16), .enable("false")) multiplexer_5 (
    .in0(regbank_1_reg0), .in1(regbank_1_reg1), .in2(regbank_1_reg2), .in3(regbank_1_reg3),
    .in4(regbank_1_reg4), .in5(regbank_1_reg5), .in6(regbank_1_reg6), .in7({regbank_1_sp_2, regbank_1_sp}),
    .out({multiplexer_5_out_2, multiplexer_5_out}), .sel(n12bitreg_1_output[5:3]));
  _12BITREG u_12bitreg_1 (.INPUT(ram_1_data[11:0]), .CLK(CLOCK), .LOAD(rom_1_data[13]), .OUTPUT(n12bitreg_1_output));
  _1BITREG u_1bitreg_1 (.CLK(CLOCK), .INPUT(alu_1_zf), .LOAD(rom_1_data[14]), .OUTPUT(n1bitreg_1_output[0]));
  Multiplexer #(.width(5), .enable("false")) multiplexer_6 (
    .in0(rom_1_data_2), .in1(multiplexer_7_out), .out(multiplexer_6_out), .sel(rom_1_data[17]));
  Multiplexer #(.select(2), .width(5), .enable("false")) multiplexer_7 (
    .in0({ram_1_data[15:12], 1'b0}), .in1({ram_1_data[15:12], 1'b0}), .in2({5{1'b0}}), .in3(5'b01010),
    .out(multiplexer_7_out), .sel(n1bitreg_1_output));
  _5BITREG u_5bitreg_1 (.INPUT(multiplexer_6_out), .CLK(CLOCK), .LOAD(1'b1), .OUTPUT(n5bitreg_1_output));
  ROM #(.addrWidth(5), .dataWidth(20)) rom_1 (
    .addr(n5bitreg_1_output), .data({rom_1_data, rom_1_data_2}));  // open: sel

  // Notes on the sheet:
  //   contents of rom_1 (hex, n*v repeats v):
  //   2a000 0 8020 0 820 0 b00 0 0 0 10000 0 0 0 4620 0 1380 0 53 1020 51180 0 57 91000
  //   Next Address
endmodule

module isJZ (
  input  [3:0] in_1,
  output jz
);

  wire not_1_out, not_2_out, not_3_out;

  not not_1 (not_1_out, in_1[0]);
  not not_2 (not_2_out, in_1[1]);
  not not_3 (not_3_out, in_1[3]);
  and and_1 (jz, not_1_out, not_2_out, in_1[2], not_3_out);
endmodule
